// Logisim project main.circ as structural Verilog: 6 circuits, main circuit main
module main (
);

  wire alu_1_out_14, alu_1_out_16, clk, jump_en, rst;
  wire [2:0] alu_1_out_13;
  wire [4:0] decode_1_out_5, decode_1_out_11, rd_addr, rs1_addr, rs2_addr;
  wire [23:0] mem_addr;
  wire [31:0] decode_1_out_9, decode_1_out_10, jump_addr, Load_data, op1, op2, pc_1_out_5, rd_data,
       register_1_out_10, register_1_out_11, riscv_probe_1_p1, rs1_data, rs2_data, write_data;

  Clock #(.highDuration(1), .lowDuration(1)) clock_1 (.out(clk));
  Button button_1 (.out(rst));
  pc pc_1 (.in_2(clk), .in_3(rst), .out_5(pc_1_out_5), .in_1(jump_addr), .in_4(jump_en));
  // Probe on pc_1_out_5
  // Probe on rs1_data
  // Probe on rd_data
  // Probe on mem_addr
  // RiscV_Probe riscv_probe_1: pin names not known; wires that end beside it: riscv_probe_1_p1
  ROM #(.addrWidth(20), .dataWidth(32), .Select("low")) rom_1 (.addr(pc_1_out_5[21:2]), .data(riscv_probe_1_p1));
  // Probe on rs2_data
  // Probe on op1
  // Probe on write_data
  decode decode_1 (
    .in_3(rs1_data), .in_4(rs2_data), .out_5(decode_1_out_5), .out_6(rs1_addr), .out_11(decode_1_out_11),
    .out_12(rs2_addr), .out_7(op1), .out_8(op2), .out_9(decode_1_out_9), .out_10(decode_1_out_10),
    .in_2(pc_1_out_5), .in_1(riscv_probe_1_p1));
  // Probe on rd_addr
  // Probe on op2
  // Probe on Load_data
  // Probe on rs1_addr
  // Probe on rs2_addr
  ALU alu_1 (
    .in_1(op1), .in_4(op2), .in_6(decode_1_out_11), .in_7(decode_1_out_5), .out_10(rd_data),
    .out_12(rd_addr), .in_2(decode_1_out_9), .in_5(decode_1_out_10), .out_9(jump_addr), .out_11(jump_en),
    .out_16(alu_1_out_16), .out_14(alu_1_out_14), .out_15(mem_addr), .out_8(write_data), .in_3(Load_data),
    .out_13(alu_1_out_13));
  register register_1 (
    .in_1(clk), .in_2(rst), .in_3(1'b1), .in_4(rd_addr), .out_8(rs1_data), .out_9(rs2_data), .in_5(rs1_addr),
    .in_6(rd_data), .in_7(rs2_addr), .out_10(register_1_out_10), .out_11(register_1_out_11));
  // Probe on register_1_out_10
  // Probe on register_1_out_11
  RAN ran_1 (
    .in_1(write_data), .in_2(alu_1_out_14), .in_3(alu_1_out_16), .out_8(Load_data), .in_4(rst),
    .in_5(mem_addr), .in_6(clk), .in_7(alu_1_out_13));

  // Notes on the sheet:
  //   contents of rom_1 (hex, n*v repeats v):
  //   d13 d93 1097 ff808093 aa0137 aa10113 20a023 af03 aa0eb7 aae8e93 200193 47df1063 1097 fd008093
  //   aa00b137 a0010113 20a223 40af03 aa00beb7 a00e8e93 300193 43df1c63 1097 fa808093 aa01137 aa010113
  //   20a423 80af03 aa01eb7 aa0e8e93 400193 41df1863 1097 f8008093 a00aa137 a10113 20a623 c0af03 a00aaeb7
  //   ae8e93 500193 3fdf1463 1097 f7408093 aa0137 aa10113 fe20aa23 ff40af03 aa0eb7 aae8e93 600193 3ddf1063
  //   1097 f4c08093 aa00b137 a0010113 fe20ac23 ff80af03 aa00beb7 a00e8e93 700193 39df1c63 1097 f2408093
  //   aa01137 aa010113 fe20ae23 ffc0af03 aa01eb7 aa0e8e93 800193 37df1863 1097 efc08093 a00aa137 a10113
  //   20a023 af03 a00aaeb7 ae8e93 900193 35df1463 1097 ed808093 12345137 67810113 fe008213 2222023 a283
  //   12345eb7 678e8e93 a00193 31d29e63 1097 eac08093 58213137 9810113 ffd08093 20a3a3 1217 e9820213 22283
  //   58213eb7 98e8e93 b00193 2fd29463 c00193 213 aabbd0b7 cdd08093 1117 e4810113 112023 12f03 aabbdeb7
  //   cdde8e93 2bdf1e63 120213 200293 fc521ae3 d00193 213 daabc0b7 ccd08093 1117 e1010113 13 112223 412f03
  //   daabceb7 ccde8e93 29df1063 120213 200293 fc5218e3 e00193 213 ddaac0b7 bcc08093 1117 dd410113 13 13
  //   112423 812f03 ddaaceb7 bcce8e93 25df1063 120213 200293 fc5216e3 f00193 213 cddab0b7 bbc08093 13 1117
  //   d9010113 112623 c12f03 cddabeb7 bbce8e93 21df1263 120213 200293 fc5218e3 1000193 213 ccddb0b7
  //   abb08093 13 1117 d5410113 13 112823 1012f03 ccddbeb7 abbe8e93 1ddf1263 120213 200293 fc5216e3
  //   1100193 213 bccde0b7 aab08093 13 13 1117 d1010113 112a23 1412f03 bccdeeb7 aabe8e93 19df1263 120213
  //   200293 fc5216e3 1200193 213 1117 ce010113 1120b7 23308093 112023 12f03 112eb7 233e8e93 15df1663
  //   120213 200293 fc521ae3 1300193 213 1117 ca810113 300110b7 22308093 13 112223 412f03 30011eb7
  //   223e8e93 11df1863 120213 200293 fc5218e3 1400193 213 1117 c6c10113 330010b7 12208093 13 13 112423
  //   812f03 33001eb7 122e8e93 ddf1863 120213 200293 fc5216e3 1500193 213 1117 c2c10113 13 233000b7
  //   11208093 112623 c12f03 23300eb7 112e8e93 9df1a63 120213 200293 fc5218e3 1600193 213 1117 bf010113 13
  //   223300b7 1108093 13 112823 1012f03 22330eb7 11e8e93 5df1a63 120213 200293 fc5216e3 1700193 213 1117
  //   bb010113 13 13 122330b7 108093 112a23 1412f03 12233eb7 1e8e93 1df1a63 120213 200293 fc5216e3 301863
  //   100d13 d93 6f 100d13 100d93 6f 727*0 10*deadbeef
endmodule

module pc (
  input  [31:0] in_1,
  input  in_2,
  input  in_3,
  input  in_4,
  output [31:0] out_5
);

  wire [31:0] adder_1_out, multiplexer_1_out;

  // Probe on adder_1_out
  Adder #(.width(32)) adder_1 (.a(out_5), .b(32'h4), .out(adder_1_out));  // open: cin, cout
  Register #(.width(32), .trigger("rising"), .Select("low")) register_1 (
    .D(multiplexer_1_out), .Q(out_5), .clk(in_2), .clr(in_3));  // open: en
  Multiplexer #(.select(1), .width(32), .disabled("Z"), .enable("false")) multiplexer_1 (
    .in0(adder_1_out), .in1(in_1), .out(multiplexer_1_out), .sel(in_4));
  // Probe on multiplexer_1_out
  // Probe on out_5

  // Other names for the same wires on the sheet: clk = in_2; jump_addr[31:0] = in_1; jump_en = in_4;
  //   out[31:0] = out_5; rst = in_3
endmodule

module decode (
  input  [31:0] in_1,
  input  [31:0] in_2,
  input  [31:0] in_3,
  input  [31:0] in_4,
  output [4:0] out_5,
  output [4:0] out_6,
  output [31:0] out_7,
  output [31:0] out_8,
  output [31:0] out_9,
  output [31:0] out_10,
  output [4:0] out_11,
  output [4:0] out_12
);

  wire ADD, ADD_I, ADD_R, AND, AND_I, AND_R, auipc, BEQ, BGE, BGEU, BLT, BLTU, BNE, i_sel, \IL类 , \I类 , jal,
       jalr, LB, LBU, LH, LHU, lui, LW, OR, OR_I, OR_R, \R类 , SB, \SB类 , SH, SLL, SLL_I, SLL_R, SLT, SLT_I,
       SLT_R, SLTU, SLTU_I, SLTU_R, SRA, SRA_I, SRA_R, SRL, SRL_I, SRL_R, SUB, SW, \S类 , XOR, XOR_I, XOR_R;
  wire [3:0] OP_SEL;
  wire [31:0] bit_extender_7_out, i_immi, IL_immi, immi_jump2, jal_immi, jalr_immi, lui_auipc_immi, S_immi;

  // Probe on in_1[31:12]
  // Probe on {in_1[31], in_1[19:12], in_1[20], in_1[30:21]}
  assign immi_jump2 = {{19{in_1[31]}}, {in_1[31], in_1[7], in_1[30:25], in_1[11:8], 1'b0}};  // Bit_Extender bit_extender_1
  assign lui_auipc_immi = {{12{in_1[31]}}, in_1[31:12]};  // Bit_Extender bit_extender_2
  assign jal_immi = {{12{in_1[31]}}, {in_1[31], in_1[19:12], in_1[20], in_1[30:21]}};  // Bit_Extender bit_extender_3
  assign jalr_immi = {{20{in_1[31]}}, in_1[31:20]};  // Bit_Extender bit_extender_4
  assign S_immi = {{20{in_1[31]}}, {in_1[31:25], in_1[11:7]}};  // Bit_Extender bit_extender_5
  Priority_Encoder #(.select(4), .disabled("Z")) priority_encoder_1 (
    .in0(\R类 ), .in1(\I类 ), .in2(\SB类 ), .in3(lui), .in4(auipc), .in5(jal), .in6(jalr), .in7(\IL类 ),
    .in8(\S类 ), .out(OP_SEL));  // open: in9, in10, in11, in12, in13, in14, in15, gs, en_out, en_in
  Multiplexer #(.select(4), .width(32), .disabled("Z"), .enable("false")) multiplexer_1 (
    .in0({32{1'b0}}), .in1({32{1'b0}}), .in2(in_2), .in3(in_2), .in4(in_2), .in5(in_2), .in6(in_2),
    .in7({32{1'b0}}), .in8({32{1'b0}}), .out(out_9), .sel(OP_SEL));  // open: in9, in10, in11, in12, in13, in14, in15
  // Probe on lui_auipc_immi
  and and_1 (\R类 , ~in_1[6], in_1[5], in_1[4], ~in_1[3], ~in_1[2], in_1[1], in_1[0]);  // AND_Gate
  and and_2 (\I类 , ~in_1[6], ~in_1[5], in_1[4], ~in_1[3], ~in_1[2], in_1[1], in_1[0]);  // AND_Gate
  and and_3 (\SB类 , in_1[6], in_1[5], ~in_1[4], ~in_1[3], ~in_1[2], in_1[1], in_1[0]);  // AND_Gate
  and and_4 (\IL类 , ~in_1[6], ~in_1[5], ~in_1[4], ~in_1[3], ~in_1[2], in_1[1], in_1[0]);  // AND_Gate
  and and_5 (\S类 , ~in_1[6], in_1[5], ~in_1[4], ~in_1[3], ~in_1[2], in_1[1], in_1[0]);  // AND_Gate
  assign IL_immi = {{20{in_1[31]}}, in_1[31:20]};  // Bit_Extender bit_extender_6
  assign bit_extender_7_out = {{27{1'b0}}, in_1[24:20]};  // Bit_Extender bit_extender_7
  and and_6 (i_sel, ~in_1[13], in_1[12]);  // AND_Gate
  // Probe on i_immi
  Multiplexer #(.select(1), .width(32), .disabled("Z"), .enable("false")) multiplexer_2 (
    .in0(IL_immi), .in1(bit_extender_7_out), .out(i_immi), .sel(i_sel));
  // Probe on immi_jump2
  and and_7 (lui, ~in_1[6], in_1[5], in_1[4], ~in_1[3], in_1[2], in_1[1], in_1[0]);  // AND_Gate
  and and_8 (jal, in_1[6], in_1[5], ~in_1[4], in_1[3], in_1[2], in_1[1], in_1[0]);  // AND_Gate
  and and_9 (auipc, ~in_1[6], ~in_1[5], in_1[4], ~in_1[3], in_1[2], in_1[1], in_1[0]);  // AND_Gate
  and and_10 (jalr, in_1[6], in_1[5], ~in_1[4], ~in_1[3], in_1[2], in_1[1], in_1[0]);  // AND_Gate
  // Probe on out_8
  Multiplexer #(.select(4), .width(32), .disabled("Z"), .enable("false")) multiplexer_3 (
    .in0(in_4), .in1(i_immi), .in2(in_4), .in3(lui_auipc_immi), .in4(lui_auipc_immi), .in5({32{1'b0}}),
    .in6({32{1'b0}}), .in7(IL_immi), .in8(S_immi), .out(out_8), .sel(OP_SEL));  // open: in9, in10, in11, in12, in13, in14, in15
  Multiplexer #(.select(4), .width(32), .disabled("Z"), .enable("false")) multiplexer_4 (
    .in0({32{1'b0}}), .in1({32{1'b0}}), .in2(immi_jump2), .in3({32{1'b0}}), .in4({32{1'b0}}), .in5(jal_immi),
    .in6(jalr_immi), .in7({32{1'b0}}), .in8(in_4), .out(out_10), .sel(OP_SEL));  // open: in9, in10, in11, in12, in13, in14, in15
  and and_11 (ADD_R, ~in_1[30], \R类 , ~in_1[14], ~in_1[13], ~in_1[12]);  // AND_Gate
  and and_12 (SUB, in_1[30], \R类 , ~in_1[14], ~in_1[13], ~in_1[12]);  // AND_Gate
  and and_13 (SLL_R, ~in_1[30], \R类 , ~in_1[14], ~in_1[13], in_1[12]);  // AND_Gate
  and and_14 (SLT_R, ~in_1[30], \R类 , ~in_1[14], in_1[13], ~in_1[12]);  // AND_Gate
  and and_15 (SLTU_R, ~in_1[30], \R类 , ~in_1[14], in_1[13], in_1[12]);  // AND_Gate
  and and_16 (XOR_R, ~in_1[30], \R类 , in_1[14], ~in_1[13], ~in_1[12]);  // AND_Gate
  and and_17 (SRL_R, ~in_1[30], \R类 , in_1[14], ~in_1[13], in_1[12]);  // AND_Gate
  and and_18 (SRA_R, in_1[30], \R类 , in_1[14], ~in_1[13], in_1[12]);  // AND_Gate
  and and_19 (OR_R, ~in_1[30], \R类 , in_1[14], in_1[13], ~in_1[12]);  // AND_Gate
  and and_20 (AND_R, ~in_1[30], \R类 , in_1[14], in_1[13], in_1[12]);  // AND_Gate
  and and_21 (BEQ, \SB类 , ~in_1[14], ~in_1[13], ~in_1[12]);  // AND_Gate
  and and_22 (BNE, \SB类 , ~in_1[14], ~in_1[13], in_1[12]);  // AND_Gate
  and and_23 (BLT, \SB类 , in_1[14], ~in_1[13], ~in_1[12]);  // AND_Gate
  and and_24 (BGE, \SB类 , in_1[14], ~in_1[13], in_1[12]);  // AND_Gate
  and and_25 (BLTU, \SB类 , in_1[14], in_1[13], ~in_1[12]);  // AND_Gate
  and and_26 (BGEU, \SB类 , in_1[14], in_1[13], in_1[12]);
  Priority_Encoder #(.select(5), .disabled("Z")) priority_encoder_2 (
    .in0(ADD), .in1(SUB), .in2(SLL), .in3(SLT), .in4(SLTU), .in5(XOR), .in6(SRL), .in7(SRA), .in8(OR),
    .in9(AND), .in10(BEQ), .in11(BNE), .in12(BLT), .in13(BGE), .in14(BLTU), .in15(BGEU), .in16(jal),
    .in17(jalr), .in18(lui), .in19(auipc), .in20(LB), .in21(LH), .in22(LW), .in23(LBU), .in24(LHU),
    .in25(SB), .in26(SH), .in27(SW), .in28(1'b0), .in29(1'b0), .in30(1'b0), .in31(1'b0), .out(out_11));  // open: gs, en_out, en_in
  or or_1 (ADD, ADD_R, ADD_I);
  or or_2 (SLL, SLL_R, SLL_I);
  or or_3 (SLT, SLT_R, SLT_I);
  or or_4 (SLTU, SLTU_R, SLTU_I);
  or or_5 (XOR, XOR_R, XOR_I);
  and and_27 (OR_I, \I类 , in_1[14], in_1[13], ~in_1[12]);  // AND_Gate
  and and_28 (AND_I, \I类 , in_1[14], in_1[13], in_1[12]);  // AND_Gate
  and and_29 (ADD_I, \I类 , ~in_1[14], ~in_1[13], ~in_1[12]);  // AND_Gate
  or or_6 (SRL, SRL_R, SRL_I);
  or or_7 (SRA, SRA_R, SRA_I);
  or or_8 (OR, OR_R, OR_I);
  or or_9 (AND, AND_R, AND_I);
  and and_30 (BEQ, \SB类 , ~in_1[14], ~in_1[13], ~in_1[12]);  // AND_Gate
  and and_31 (BNE, \SB类 , ~in_1[14], ~in_1[13], in_1[12]);  // AND_Gate
  and and_32 (BLT, \SB类 , in_1[14], ~in_1[13], ~in_1[12]);  // AND_Gate
  and and_33 (BGE, \SB类 , in_1[14], ~in_1[13], in_1[12]);  // AND_Gate
  and and_34 (BLTU, \SB类 , in_1[14], in_1[13], ~in_1[12]);  // AND_Gate
  and and_35 (BGEU, \SB类 , in_1[14], in_1[13], in_1[12]);
  and and_36 (LB, \IL类 , ~in_1[14], ~in_1[13], ~in_1[12]);  // AND_Gate
  and and_37 (LH, \IL类 , ~in_1[14], ~in_1[13], in_1[12]);  // AND_Gate
  and and_38 (LW, \IL类 , ~in_1[14], in_1[13], ~in_1[12]);  // AND_Gate
  and and_39 (LBU, \IL类 , in_1[14], ~in_1[13], ~in_1[12]);  // AND_Gate
  and and_40 (LHU, \IL类 , in_1[14], ~in_1[13], in_1[12]);  // AND_Gate
  and and_41 (SLT_I, \I类 , ~in_1[14], in_1[13], ~in_1[12]);  // AND_Gate
  and and_42 (SLTU_I, \I类 , ~in_1[14], in_1[13], in_1[12]);  // AND_Gate
  and and_43 (XOR_I, \I类 , in_1[14], ~in_1[13], ~in_1[12]);  // AND_Gate
  and and_44 (SB, \S类 , ~in_1[14], ~in_1[13], ~in_1[12]);  // AND_Gate
  and and_45 (SH, \S类 , ~in_1[14], ~in_1[13], in_1[12]);  // AND_Gate
  and and_46 (SW, \S类 , ~in_1[14], in_1[13], ~in_1[12]);  // AND_Gate
  and and_47 (SLL_I, ~in_1[30], \I类 , ~in_1[14], ~in_1[13], in_1[12]);  // AND_Gate
  and and_48 (SRL_I, ~in_1[30], \I类 , in_1[14], ~in_1[13], in_1[12]);  // AND_Gate
  and and_49 (SRA_I, in_1[30], \I类 , in_1[14], ~in_1[13], in_1[12]);  // AND_Gate

  assign out_5 = in_1[11:7];
  assign out_6 = in_1[19:15];
  assign out_7 = in_3;
  assign out_12 = in_1[24:20];

  // Other names for the same wires on the sheet: instr[31:0] = in_1; rd[4:0] = in_1[11:7]; rs2[4:0] = in_1[24:20];
  //   funct7[6:0] = in_1[31:25]; flag = in_1[30]; funct3[2:0] = in_1[14:12]; rs1[4:0] = in_1[19:15];
  //   immi_jump1[31:0] = in_2; opcode[6:0] = in_1[6:0]; jump_op1[31:0] = out_9; jump_op2[31:0] = out_10;
  //   op2[31:0] = out_8; op1[31:0] = in_3; rs1_data[31:0] = in_3; rs2_data[31:0] = in_4; sel[4:0] = out_11

  // Notes on the sheet:
  //   pc_addr
  //   0110011
  //   0010011
  //   1100011
  //   jalr
  //   S类
  //   lui/auipc
  //   jal
  //   0110111
  //   1101111
  //   0010111
  //   1100111
  //   I类
  //   SB类/S类
  //   R类
  //   decode
  //   SB类
  //   IL类/S类
  //   输入
  //   输出
  //   RI类
  //   U/J类
endmodule

module ALU (
  input  [31:0] in_1,
  input  [31:0] in_2,
  input  [31:0] in_3,
  input  [31:0] in_4,
  input  [31:0] in_5,
  input  [4:0] in_6,
  input  [4:0] in_7,
  output [31:0] out_8,
  output [31:0] out_9,
  output [31:0] out_10,
  output out_11,
  output [4:0] out_12,
  output [2:0] out_13,
  output out_14,
  output [23:0] out_15,
  output out_16
);

  wire comparator_3_eq, comparator_4_eq, comparator_5_lt, comparator_6_gt, comparator_7_lt, comparator_8_gt,
       comparator_9_gt, comparator_10_lt, comparator_11_gt, comparator_12_lt, comparator_13_gt,
       comparator_14_lt, not_1_out, sel_en;
  wire [0:0] comparator_1_lt, comparator_2_lt;
  wire [3:0] jump_sel;
  wire [4:3] subtractor_3_out;
  wire [4:4] subtractor_2_out;
  wire [31:0] adder_1_out, adder_2_out, adder_3_out, adder_4_out, adder_6_out, and_1_out, and_3_out,
       bit_extender_1_out, bit_extender_2_out, bit_extender_3_out, bit_extender_4_out, bit_extender_5_out,
       bit_extender_6_out, jump_op, multiplexer_2_out, multiplexer_3_out, multiplexer_4_out,
       multiplexer_5_out, multiplexer_6_out, multiplexer_7_out, or_1_out, shifter_1_out, shifter_2_out,
       shifter_3_out, shifter_4_out, shifter_5_out, subtractor_1_out, xor_1_out;
  wire [31:24] adder_7_out;

  Adder #(.width(32)) adder_1 (.a(in_1), .b(in_4), .out(adder_1_out));  // open: cin, cout
  Subtractor #(.width(32)) subtractor_1 (.a(in_1), .b(in_4), .out(subtractor_1_out));  // open: bin, bout
  Shifter #(.width(32), .shift("ll")) shifter_1 (.in(in_1), .\dist (in_4[4:0]), .out(shifter_1_out));
  Comparator #(.width(32), .mode("twosComplement")) comparator_1 (
    .a(in_1), .b(in_4), .lt(comparator_1_lt[0]));  // open: gt, eq
  Comparator #(.width(32), .mode("unsigned")) comparator_2 (
    .a(in_1), .b(in_4), .lt(comparator_2_lt[0]));  // open: gt, eq
  assign xor_1_out = in_1 ^ in_4;  // XOR_Gate xor_1, 32 bits wide
  Shifter #(.width(32), .shift("lr")) shifter_2 (.in(in_1), .\dist (in_4[4:0]), .out(shifter_2_out));
  Shifter #(.width(32), .shift("ar")) shifter_3 (.in(in_1), .\dist (in_4[4:0]), .out(shifter_3_out));
  assign or_1_out = in_1 | in_4;  // OR_Gate or_1, 32 bits wide
  assign and_1_out = in_1 & in_4;  // AND_Gate and_1, 32 bits wide
  Shifter #(.width(32), .shift("ll")) shifter_4 (.in(in_4), .\dist (5'b01100), .out(shifter_4_out));
  assign bit_extender_1_out = {{24{in_3[7]}}, in_3[7:0]};  // Bit_Extender bit_extender_1
  assign bit_extender_2_out = {{16{in_3[15]}}, in_3[15:0]};  // Bit_Extender bit_extender_2
  assign bit_extender_3_out = {{24{1'b0}}, in_3[7:0]};  // Bit_Extender bit_extender_3
  assign bit_extender_4_out = {{16{1'b0}}, in_3[15:0]};  // Bit_Extender bit_extender_4
  // Probe on adder_1_out
  Adder #(.width(32)) adder_2 (.a(in_2), .b(32'h4), .out(adder_2_out));  // open: cin, cout
  Adder #(.width(32)) adder_3 (.a(in_2), .b(32'h4), .out(adder_3_out));  // open: cin, cout
  Shifter #(.width(32), .shift("ll")) shifter_5 (.in(in_4), .\dist (5'b01100), .out(shifter_5_out));
  Adder #(.width(32)) adder_4 (.a(shifter_4_out), .b(in_2), .out(adder_4_out));  // open: cin, cout
  // Probe on out_10
  Multiplexer #(.select(5), .width(32), .disabled("Z"), .enable("false")) multiplexer_1 (
    .in0(adder_1_out), .in1(subtractor_1_out), .in2(shifter_1_out), .in3({{31{1'b0}}, comparator_1_lt[0]}),
    .in4({{31{1'b0}}, comparator_2_lt[0]}), .in5(xor_1_out), .in6(shifter_2_out), .in7(shifter_3_out),
    .in8(or_1_out), .in9(and_1_out), .in10({32{1'b0}}), .in11({32{1'b0}}), .in12({32{1'b0}}),
    .in13({32{1'b0}}), .in14({32{1'b0}}), .in15({32{1'b0}}), .in16(adder_2_out), .in17(adder_3_out),
    .in18(shifter_5_out), .in19(adder_4_out), .in20(bit_extender_1_out), .in21(bit_extender_2_out),
    .in22(in_3), .in23(bit_extender_3_out), .in24(bit_extender_4_out), .in28({32{1'b0}}), .in29({32{1'b0}}),
    .in30({32{1'b0}}), .in31({32{1'b0}}), .out(out_10), .sel(in_6));  // open: in25, in26, in27
  // Probe on in_6
  // Probe on in_6
  Comparator #(.width(32), .mode("twosComplement")) comparator_3 (
    .a(in_1), .b(in_4), .eq(comparator_3_eq));  // open: gt, lt
  Comparator #(.width(32), .mode("twosComplement")) comparator_4 (
    .a(in_1), .b(in_4), .eq(comparator_4_eq));  // open: gt, lt
  not not_1 (not_1_out, comparator_4_eq);
  Comparator #(.width(32), .mode("twosComplement")) comparator_5 (
    .a(in_1), .b(in_4), .lt(comparator_5_lt));  // open: gt, eq
  Comparator #(.width(32), .mode("twosComplement")) comparator_6 (
    .a(in_1), .b(in_4), .gt(comparator_6_gt));  // open: eq, lt
  Comparator #(.width(32), .mode("unsigned")) comparator_7 (.a(in_1), .b(in_4), .lt(comparator_7_lt));  // open: gt, eq
  Comparator #(.width(32), .mode("unsigned")) comparator_8 (.a(in_1), .b(in_4), .gt(comparator_8_gt));  // open: eq, lt
  Subtractor #(.width(5)) subtractor_2 (
    .a(in_6), .b(5'b01010), .out({subtractor_2_out[4], jump_sel}));  // open: bin, bout
  Comparator #(.width(5), .mode("unsigned")) comparator_9 (
    .a(in_6), .b(5'b01001), .gt(comparator_9_gt));  // open: eq, lt
  Comparator #(.width(6), .mode("unsigned")) comparator_10 (
    .a({1'b0, in_6}), .b(6'b010010), .lt(comparator_10_lt));  // open: gt, eq
  Adder #(.width(32)) adder_5 (.a(in_2), .b(in_5), .out(jump_op));  // open: cin, cout
  // Probe on in_1
  and and_2 (sel_en, comparator_9_gt, comparator_10_lt);
  Multiplexer #(.select(1), .width(32), .disabled("Z"), .enable("false")) multiplexer_2 (
    .in0({32{1'b0}}), .in1(jump_op), .out(multiplexer_2_out), .sel(comparator_3_eq));
  Multiplexer #(.select(1), .width(32), .disabled("Z"), .enable("false")) multiplexer_3 (
    .in0({32{1'b0}}), .in1(jump_op), .out(multiplexer_3_out), .sel(not_1_out));
  Multiplexer #(.select(1), .width(32), .disabled("Z"), .enable("false")) multiplexer_4 (
    .in0({32{1'b0}}), .in1(jump_op), .out(multiplexer_4_out), .sel(comparator_5_lt));
  Multiplexer #(.select(1), .width(32), .disabled("Z"), .enable("false")) multiplexer_5 (
    .in0({32{1'b0}}), .in1(jump_op), .out(multiplexer_5_out), .sel(comparator_6_gt));
  Multiplexer #(.select(1), .width(32), .disabled("Z"), .enable("false")) multiplexer_6 (
    .in0({32{1'b0}}), .in1(jump_op), .out(multiplexer_6_out), .sel(comparator_7_lt));
  Multiplexer #(.select(1), .width(32), .disabled("Z"), .enable("false")) multiplexer_7 (
    .in0({32{1'b0}}), .in1(jump_op), .out(multiplexer_7_out), .sel(comparator_8_gt));
  Adder #(.width(32)) adder_6 (.a(in_1), .b(in_5), .out(adder_6_out));  // open: cin, cout
  Multiplexer #(.select(4), .width(1), .disabled(0), .enable("true")) multiplexer_8 (
    .in0(comparator_3_eq), .in1(not_1_out), .in2(comparator_5_lt), .in3(comparator_6_gt),
    .in4(comparator_7_lt), .in5(comparator_8_gt), .in6(1'b1), .in7(1'b1), .in8(1'b0), .in9(1'b0),
    .in10(1'b0), .in11(1'b0), .in12(1'b0), .in13(1'b0), .in14(1'b0), .in15(1'b0), .out(out_11),
    .sel(jump_sel), .en(sel_en));
  assign and_3_out = adder_6_out & 32'hfffffffe;  // AND_Gate and_3, 32 bits wide
  Multiplexer #(.select(4), .width(32), .disabled("Z"), .enable("false")) multiplexer_9 (
    .in0(multiplexer_2_out), .in1(multiplexer_3_out), .in2(multiplexer_4_out), .in3(multiplexer_5_out),
    .in4(multiplexer_6_out), .in5(multiplexer_7_out), .in6(jump_op), .in7(and_3_out), .in8({32{1'b0}}),
    .in9({32{1'b0}}), .in10({32{1'b0}}), .in11({32{1'b0}}), .in12({32{1'b0}}), .in13({32{1'b0}}),
    .in14({32{1'b0}}), .in15({32{1'b0}}), .out(out_9), .sel(jump_sel));
  Multiplexer #(.select(5), .width(5), .disabled("Z"), .enable("false")) multiplexer_10 (
    .in0(in_7), .in1(in_7), .in2(in_7), .in3(in_7), .in4(in_7), .in5(in_7), .in6(in_7), .in7(in_7),
    .in8(in_7), .in9(in_7), .in10({5{1'b0}}), .in11({5{1'b0}}), .in12({5{1'b0}}), .in13({5{1'b0}}),
    .in14({5{1'b0}}), .in15({5{1'b0}}), .in16(in_7), .in17(in_7), .in18(in_7), .in19(in_7), .in20(in_7),
    .in21(in_7), .in22(in_7), .in23(in_7), .in24(in_7), .in25({5{1'b0}}), .in26({5{1'b0}}), .in27({5{1'b0}}),
    .out(out_12), .sel(in_6));  // open: in28, in29, in30, in31
  // Probe on in_4
  assign bit_extender_5_out = {{24{1'b0}}, in_5[7:0]};  // Bit_Extender bit_extender_5
  assign bit_extender_6_out = {{16{1'b0}}, in_5[15:0]};  // Bit_Extender bit_extender_6
  Adder #(.width(32)) adder_7 (.a(in_4), .b(in_1), .out({adder_7_out, out_15}));  // open: cin, cout
  // Probe on in_1
  // Probe on in_6
  Subtractor #(.width(5)) subtractor_3 (.a(in_6), .b(5'b10100), .out({subtractor_3_out, out_13}));  // open: bin, bout
  Multiplexer #(.select(3), .width(32), .disabled("Z"), .enable("false")) multiplexer_11 (
    .in0({32{1'b0}}), .in1({32{1'b0}}), .in2({32{1'b0}}), .in3({32{1'b0}}), .in4({32{1'b0}}),
    .in5(bit_extender_5_out), .in6(bit_extender_6_out), .in7(in_5), .out(out_8), .sel(out_13));
  // Probe on in_6
  // Probe on in_6
  Comparator #(.width(5), .mode("unsigned")) comparator_11 (
    .a(in_6), .b(5'b10011), .gt(comparator_11_gt));  // open: eq, lt
  Comparator #(.width(6), .mode("unsigned")) comparator_12 (
    .a({1'b0, in_6}), .b(6'b010111), .lt(comparator_12_lt));  // open: gt, eq
  Comparator #(.width(5), .mode("unsigned")) comparator_13 (
    .a(in_6), .b(5'b11000), .gt(comparator_13_gt));  // open: eq, lt
  Comparator #(.width(6), .mode("unsigned")) comparator_14 (
    .a({1'b0, in_6}), .b(6'b011101), .lt(comparator_14_lt));  // open: gt, eq
  and and_4 (out_16, comparator_11_gt, comparator_12_lt);
  and and_5 (out_14, comparator_13_gt, comparator_14_lt);

  // Other names for the same wires on the sheet: ran_addr[23:0] = out_15; IL_S_sel[2:0] = out_13; sel[4:0] = in_6;
  //   jump_addr[31:0] = out_9; jump_en = out_11; jump_op1[31:0] = in_2; jump_op2[31:0] = in_5; Load_data[31:0] = in_3;
  //   Load_en = out_16; op1[31:0] = in_1; op2[31:0] = in_4; rd_addr[4:0] = in_7; rd_addr_out[4:0] = out_12;
  //   rd_data[31:0] = out_10; write_data[31:0] = out_8; write_en = out_14

  // Notes on the sheet:
  //   RI类
  //   输入
  //   输出
  //   SB类
  //   U类、J类
  //   IL类、S类
endmodule

module register (
  input  in_1,
  input  in_2,
  input  in_3,
  input  [4:0] in_4,
  input  [4:0] in_5,
  input  [31:0] in_6,
  input  [4:0] in_7,
  output [31:0] out_8,
  output [31:0] out_9,
  output [31:0] out_10,
  output [31:0] out_11
);

  wire [31:0] din0, din1, din2, din3, din4, din5, din6, din7, din8, din9, din10, din11, din12, din13, din14,
       din15, din16, din17, din18, din19, din20, din21, din22, din23, din24, din25, din26, din27, din28,
       din29, din30, din31, dout0, dout1, dout2, dout3, dout4, dout5, dout6, dout7, dout8, dout9, dout10,
       dout11, dout12, dout13, dout14, dout15, dout16, dout17, dout18, dout19, dout20, dout21, dout22,
       dout23, dout24, dout25, dout28, dout29, dout30, dout31;

  Demultiplexer #(.select(5), .width(32), .tristate("true"), .disabled("Z"), .enable("false")) demultiplexer_1 (
    .out0(din0), .out1(din1), .out2(din2), .out3(din3), .out4(din4), .out5(din5), .out6(din6), .out7(din7),
    .out8(din8), .out9(din9), .out10(din10), .out11(din11), .out12(din12), .out13(din13), .out14(din14),
    .out15(din15), .out16(din16), .out17(din17), .out18(din18), .out19(din19), .out20(din20), .out21(din21),
    .out22(din22), .out23(din23), .out24(din24), .out25(din25), .out26(din26), .out27(din27), .out28(din28),
    .out29(din29), .out30(din30), .out31(din31), .in(in_6), .sel(in_4));
  Register #(.width(32), .trigger("rising"), .Select("low")) register_1 (
    .en(in_3), .Q(dout0), .clk(in_1), .clr(in_2));  // open: D
  Register #(.width(32), .trigger("rising"), .Select("low")) register_2 (
    .D(din8), .en(in_3), .Q(dout8), .clk(in_1), .clr(in_2));
  Register #(.width(32), .trigger("rising"), .Select("low")) register_3 (
    .D(din16), .en(in_3), .Q(dout16), .clk(in_1), .clr(in_2));
  Register #(.width(32), .trigger("rising"), .Select("low")) register_4 (
    .D(din24), .en(in_3), .Q(dout24), .clk(in_1), .clr(in_2));
  // Probe on dout24
  // Probe on dout0
  Register #(.width(32), .trigger("rising"), .Select("low")) register_5 (
    .D(din1), .en(in_3), .Q(dout1), .clk(in_1), .clr(in_2));
  // Probe on dout1
  Register #(.width(32), .trigger("rising"), .Select("low")) register_6 (
    .D(din9), .en(in_3), .Q(dout9), .clk(in_1), .clr(in_2));
  Register #(.width(32), .trigger("rising"), .Select("low")) register_7 (
    .D(din17), .en(in_3), .Q(dout17), .clk(in_1), .clr(in_2));
  Register #(.width(32), .trigger("rising"), .Select("low")) register_8 (
    .D(din25), .en(in_3), .Q(dout25), .clk(in_1), .clr(in_2));
  Register #(.width(32), .trigger("rising"), .Select("low")) register_9 (
    .D(din2), .en(in_3), .Q(dout2), .clk(in_1), .clr(in_2));
  Register #(.width(32), .trigger("rising"), .Select("low")) register_10 (
    .D(din10), .en(in_3), .Q(dout10), .clk(in_1), .clr(in_2));
  Register #(.width(32), .trigger("rising"), .Select("low")) register_11 (
    .D(din18), .en(in_3), .Q(dout18), .clk(in_1), .clr(in_2));
  Register #(.width(32), .trigger("rising"), .Select("low")) register_12 (
    .D(din26), .en(in_3), .Q(out_10), .clk(in_1), .clr(in_2));
  Register #(.width(32), .trigger("rising"), .Select("low")) register_13 (
    .D(din3), .en(in_3), .Q(dout3), .clk(in_1), .clr(in_2));
  // Probe on dout3
  Register #(.width(32), .trigger("rising"), .Select("low")) register_14 (
    .D(din11), .en(in_3), .Q(dout11), .clk(in_1), .clr(in_2));
  Register #(.width(32), .trigger("rising"), .Select("low")) register_15 (
    .D(din19), .en(in_3), .Q(dout19), .clk(in_1), .clr(in_2));
  Register #(.width(32), .trigger("rising"), .Select("low")) register_16 (
    .D(din27), .en(in_3), .Q(out_11), .clk(in_1), .clr(in_2));
  Register #(.width(32), .trigger("rising"), .Select("low")) register_17 (
    .D(din4), .en(in_3), .Q(dout4), .clk(in_1), .clr(in_2));
  Register #(.width(32), .trigger("rising"), .Select("low")) register_18 (
    .D(din12), .en(in_3), .Q(dout12), .clk(in_1), .clr(in_2));
  Register #(.width(32), .trigger("rising"), .Select("low")) register_19 (
    .D(din20), .en(in_3), .Q(dout20), .clk(in_1), .clr(in_2));
  Register #(.width(32), .trigger("rising"), .Select("low")) register_20 (
    .D(din28), .en(in_3), .Q(dout28), .clk(in_1), .clr(in_2));
  Register #(.width(32), .trigger("rising"), .Select("low")) register_21 (
    .D(din5), .en(in_3), .Q(dout5), .clk(in_1), .clr(in_2));
  // Probe on dout5
  Register #(.width(32), .trigger("rising"), .Select("low")) register_22 (
    .D(din13), .en(in_3), .Q(dout13), .clk(in_1), .clr(in_2));
  Register #(.width(32), .trigger("rising"), .Select("low")) register_23 (
    .D(din21), .en(in_3), .Q(dout21), .clk(in_1), .clr(in_2));
  Register #(.width(32), .trigger("rising"), .Select("low")) register_24 (
    .D(din29), .en(in_3), .Q(dout29), .clk(in_1), .clr(in_2));
  Register #(.width(32), .trigger("rising"), .Select("low")) register_25 (
    .D(din6), .en(in_3), .Q(dout6), .clk(in_1), .clr(in_2));
  Register #(.width(32), .trigger("rising"), .Select("low")) register_26 (
    .D(din14), .en(in_3), .Q(dout14), .clk(in_1), .clr(in_2));
  Register #(.width(32), .trigger("rising"), .Select("low")) register_27 (
    .D(din22), .en(in_3), .Q(dout22), .clk(in_1), .clr(in_2));
  Register #(.width(32), .trigger("rising"), .Select("low")) register_28 (
    .D(din30), .en(in_3), .Q(dout30), .clk(in_1), .clr(in_2));
  // Probe on dout6
  // Probe on dout30
  Register #(.width(32), .trigger("rising"), .Select("low")) register_29 (
    .D(din7), .en(in_3), .Q(dout7), .clk(in_1), .clr(in_2));
  Register #(.width(32), .trigger("rising"), .Select("low")) register_30 (
    .D(din15), .en(in_3), .Q(dout15), .clk(in_1), .clr(in_2));
  Register #(.width(32), .trigger("rising"), .Select("low")) register_31 (
    .D(din23), .en(in_3), .Q(dout23), .clk(in_1), .clr(in_2));
  Register #(.width(32), .trigger("rising"), .Select("low")) register_32 (
    .D(din31), .en(in_3), .Q(dout31), .clk(in_1), .clr(in_2));
  Multiplexer #(.select(5), .width(32), .disabled("Z"), .enable("false")) multiplexer_1 (
    .in0(dout0), .in1(dout1), .in2(dout2), .in3(dout3), .in4(dout4), .in5(dout5), .in6(dout6), .in7(dout7),
    .in8(dout8), .in9(dout9), .in10(dout10), .in11(dout11), .in12(dout12), .in13(dout13), .in14(dout14),
    .in15(dout15), .in16(dout16), .in17(dout17), .in18(dout18), .in19(dout19), .in20(dout20), .in21(dout21),
    .in22(dout22), .in23(dout23), .in24(dout24), .in25(dout25), .in26(out_10), .in27(out_11), .in28(dout28),
    .in29(dout29), .in30(dout30), .in31(dout31), .out(out_8), .sel(in_5));
  Multiplexer #(.select(5), .width(32), .disabled("Z"), .enable("false")) multiplexer_2 (
    .in0(dout0), .in1(dout1), .in2(dout2), .in3(dout3), .in4(dout4), .in5(dout5), .in6(dout6), .in7(dout7),
    .in8(dout8), .in9(dout9), .in10(dout10), .in11(dout11), .in12(dout12), .in13(dout13), .in14(dout14),
    .in15(dout15), .in16(dout16), .in17(dout17), .in18(dout18), .in19(dout19), .in20(dout20), .in21(dout21),
    .in22(dout22), .in23(dout23), .in24(dout24), .in25(dout25), .in26(out_10), .in27(out_11), .in28(dout28),
    .in29(dout29), .in30(dout30), .in31(dout31), .out(out_9), .sel(in_7));

  // Other names for the same wires on the sheet: clk = in_1; din[31:0] = in_6; dout26[31:0] = out_10;
  //   dout27[31:0] = out_11; en = in_3; rs1_adddr[4:0] = in_5; rs1_data[31:0] = out_8; rs2_adddr[4:0] = in_7;
  //   rs2_data[31:0] = out_9; rst = in_2; wr_adddr[4:0] = in_4

  // Notes on the sheet:
  //   register
  //   zero
  //   s0/fp
  //   a6
  //   s8
  //   ra
  //   s1
  //   a7
  //   s9
  //   Sp
  //   a0
  //   s2
  //   s10
  //   输入
  //   gp
  //   a1
  //   s3
  //   s11
  //   tp
  //   a2
  //   s4
  //   t3
  //   输出
  //   t0
  //   a3
  //   s5
  //   t4
  //   t1
  //   a4
  //   s6
  //   t5
  //   t2
  //   a5
  //   s7
  //   t6
endmodule

module RAN (
  input  [31:0] in_1,
  input  in_2,
  input  in_3,
  input  in_4,
  input  [23:0] in_5,
  input  in_6,
  input  [2:0] in_7,
  output [31:0] out_8
);

  wire [31:0] multiplexer_1_out, out;

  Multiplexer #(.select(3), .width(32), .disabled(0), .enable("false")) multiplexer_1 (
    .in0({32{1'b0}}), .in1({32{1'b0}}), .in2({32{1'b0}}), .in3({32{1'b0}}), .in4({32{1'b0}}),
    .in5({out[31:8], in_1[7:0]}), .in6({out[31:16], in_1[15:0]}), .in7(in_1), .out(multiplexer_1_out),
    .sel(in_7));
  // Probe on multiplexer_1_out
  // Probe on out
  RAM #(.addrWidth(24), .dataWidth(32), .bus("separate"), .Select("low")) ram_1 (
    .addr(in_5), .din(multiplexer_1_out), .data(out), .str(in_2), .sel(1'b0), .clk(in_6), .ld(1'b1),
    .clr(in_4));
  Multiplexer #(.select(3), .width(32), .disabled(0), .enable("true")) multiplexer_2 (
    .in0(out), .in1(out), .in2(out), .in3(out), .in4(out), .in5({32{1'b0}}), .in6({32{1'b0}}),
    .in7({32{1'b0}}), .out(out_8), .sel(in_7), .en(in_3));

  // Other names for the same wires on the sheet: write_data[31:0] = in_1; addr[23:0] = in_5; clk = in_6;
  //   IL_S_sel[2:0] = in_7; load_data[31:0] = out_8; Load_en = in_3; rst = in_4; write_en = in_2

  // Notes on the sheet:
  //   输入
  //   输出
endmodule
